# Fritzing sketch Big Button (saved by Fritzing 0.9.3b)
circuit board: 8.47cm x 9cm
breadboards: 1

parts:
  S1 = Round Pushbutton
  S2 = Round Pushbutton
  S3 = Round Pushbutton
  S4 = Round Pushbutton
  S5 = Round Pushbutton
  R4 = Resistor [tolerance=±5% resistance=10k package=THT]
  R5 = Resistor [tolerance=±5% resistance=10k package=THT]
  Brain = Arduino Nano (Rev3.0)
  R2 = Resistor [tolerance=±5% resistance=10k package="0805 [SMD]"]
  R3 = Resistor [tolerance=±5% resistance=10k package="0805 [SMD]"]
  R1 = Resistor [tolerance=±5% resistance=10k package="0805 [SMD]"]
  LED1 = LED - 5mm [color="Red (633nm)" package="5 mm [THT]"]
  R6 = Resistor [tolerance=±5% resistance=220 package="0805 [SMD]"]
  LED2 = LED - 5mm [color="Red (633nm)" package="5 mm [THT]"]
  R7 = Resistor [tolerance=±5% resistance=220 package="0805 [SMD]"]
  LED3 = LED - 5mm [color="Red (633nm)" package="5 mm [THT]"]
  R8 = Resistor [tolerance=±5% resistance=220 package="0805 [SMD]"]
  LED4 = LED - 5mm [color="Red (633nm)" package="5 mm [THT]"]
  R9 = Resistor [tolerance=±5% resistance=220 package="0805 [SMD]"]
  LED5 = LED - 5mm [color="Red (633nm)" package="5 mm [THT]"]
  LED6 = LED - 5mm [color="Red (633nm)" package="5 mm [THT]"]
  LED7 = LED - 5mm [color="Red (633nm)" package="5 mm [THT]"]
  LED8 = LED - 5mm [color="Red (633nm)" package="5 mm [THT]"]
  R10 = Resistor [tolerance=±5% resistance=220 package="0805 [SMD]"]
  R11 = Resistor [tolerance=±5% resistance=220 package="0805 [SMD]"]
  R12 = Resistor [tolerance=±5% resistance=220 package="0805 [SMD]"]
  R13 = Resistor [tolerance=±5% resistance=220 package="0805 [SMD]"]
  switch = MICROWRAVE
  R17 = Resistor [tolerance=±5% resistance=2k package=THT]
  R16 = Resistor [tolerance=±5% resistance=2k package=THT]
  R15 = Resistor [tolerance=±5% resistance=2k package=THT]
  R14 = Resistor [tolerance=±5% resistance=2k package=THT]
  R18 = Resistor [tolerance=±5% resistance=2k package=THT]
  R19 = Resistor [tolerance=±5% resistance=2k package=THT]
  R20 = Resistor [tolerance=±5% resistance=2k package=THT]
  R21 = Resistor [tolerance=±5% resistance=2k package=THT]
  J1 = MICROWRAVE
  J4 = MICROWRAVE
  J9 = MICROWRAVE
  J6 = MICROWRAVE
  J5 = MICROWRAVE
  J8 = MICROWRAVE
  J2 = MICROWRAVE
  J7 = MICROWRAVE
  J3 = MICROWRAVE
  U1 = POT [package=alps_pot]  # not connected
  U2 = POT [package=alps_pot]  # not connected

nets:
  momentary A: S1.leg0, Brain.D7, R1.Pin_1
  N1: S1.leg1, S2.leg1, S3.leg1, S4.leg1, S5.leg1
  momentary B: S2.leg0, Brain.D6, R2.Pin_1
  momentary C: S3.leg0, Brain.D5, R3.Pin_1
  momentary D: S4.leg0, R4.Pin_1, Brain.D4
  momentary E: S5.leg0, R5.Pin_1, Brain.D3
  GND: R4.Pin_0, R5.Pin_0, Brain.GND, R2.Pin_0, R3.Pin_0, R1.Pin_0, LED3.cathode, switch.connector8, R21.Pin_0, J4.connector0
  N2: Brain.D2, J1.connector2
  5V: Brain.VIN
  5V Reference: Brain.5V, R14.Pin_1
  channel select: Brain.A0, switch.connector0
  N3: LED1.cathode, J2.connector0
  N4: LED1.anode, R6.Pin_0
  N5: R6.Pin_1, J2.connector2
  N6: LED2.cathode, J3.connector0
  N7: LED2.anode, R7.Pin_0
  N8: R7.Pin_1, J3.connector2
  N9: LED3.anode, R8.Pin_0
  N10: R8.Pin_1, J4.connector2
  N11: LED4.cathode, J5.connector0
  N12: LED4.anode, R9.Pin_0
  N13: R9.Pin_1, J5.connector2
  N14: LED5.cathode, J6.connector0
  N15: LED5.anode, R10.Pin_0
  N16: LED6.cathode, J9.connector0
  N17: LED6.anode, R12.Pin_0
  N18: LED7.cathode, J8.connector0
  N19: LED7.anode, R13.Pin_0
  N20: LED8.cathode, J7.connector0
  N21: LED8.anode, R11.Pin_0
  N22: R10.Pin_1, J6.connector2
  N23: R11.Pin_1, J7.connector2
  N24: R12.Pin_1, J9.connector2
  N25: R13.Pin_1, J8.connector2
  N26: switch.connector1, R15.Pin_1, R14.Pin_0
  N27: switch.connector2, R16.Pin_1, R15.Pin_0
  N28: switch.connector3, R17.Pin_1, R16.Pin_0
  N29: switch.connector4, R17.Pin_0, R18.Pin_1
  N30: switch.connector5, R18.Pin_0, R19.Pin_1
  N31: switch.connector6, R19.Pin_0, R20.Pin_1
  N32: switch.connector7, R20.Pin_0, R21.Pin_1

notes:
  The number of functions is either
  * combining: 2^(button count) = 32
  * cascading: 15-ish?
